// Logisim project Shift Register - SL, SR and LOAD.circ as structural Verilog: 1 circuit, main circuit main
module main (
  input  Lin,
  input  D0,
  input  D1,
  input  D2,
  input  Rin,
  input  S1,
  input  S0,
  input  D3
);

  wire CLK_out, multiplexer_1_out, multiplexer_2_out, multiplexer_3_out, multiplexer_4_out, Q0, Q1, Q2, Q3;

  Multiplexer #(.select(2)) multiplexer_1 (
    .in0(Q0), .in1(Q1), .in2(Lin), .in3(D0), .out(multiplexer_1_out), .sel({S1, S0}));  // open: en
  Multiplexer #(.select(2)) multiplexer_2 (
    .in0(Q1), .in1(Q2), .in2(Q0), .in3(D1), .out(multiplexer_2_out), .sel({S1, S0}));  // open: en
  Multiplexer #(.select(2)) multiplexer_3 (
    .in0(Q2), .in1(Q3), .in2(Q1), .in3(D2), .out(multiplexer_3_out), .sel({S1, S0}));  // open: en
  Multiplexer #(.select(2)) multiplexer_4 (
    .in0(Q3), .in1(Rin), .in2(Q2), .in3(D3), .out(multiplexer_4_out), .sel({S1, S0}));  // open: en
  Clock CLK (.out(CLK_out));
  D_Flip_Flop u_Q0 (.clk(CLK_out), .D(multiplexer_1_out), .Q(Q0));  // open: Qn, preset, en, reset
  LED led_1 (.in(Q0));
  D_Flip_Flop d_ff_1 (.clk(CLK_out), .D(multiplexer_2_out), .Q(Q1));  // open: Qn, preset, en, reset
  LED led_2 (.in(Q1));
  LED led_3 (.in(Q2));
  D_Flip_Flop d_ff_2 (.clk(CLK_out), .D(multiplexer_3_out), .Q(Q2));  // open: Qn, preset, en, reset
  LED led_4 (.in(Q3));
  D_Flip_Flop d_ff_3 (.clk(CLK_out), .D(multiplexer_4_out), .Q(Q3));  // open: Qn, preset, en, reset

  // Other names for the same wires on the sheet: S1S0[1:0] = {S1, S0}

  // Notes on the sheet:
  //   registrador de deslocamento  com - SHIFT LEFT e LOAD
endmodule
