// Logisim project Multiplicador de 3 bits.circ as structural Verilog: 1 circuit, main circuit main
module main (
  input  X2,
  input  X1,
  input  X0,
  input  Y2,
  input  Y1,
  input  Y0,
  output P5,
  output P4,
  output P3,
  output P2,
  output P1,
  output P0
);

  wire adder_1_cout, adder_2_cout, adder_2_out, adder_3_cout, adder_3_out, adder_5_cout, adder_6_cout,
       and_1_out, and_3_out, and_4_out, and_5_out, and_6_out, and_7_out, and_8_out, and_9_out;

  and and_1 (and_1_out, X0, Y2);
  and and_2 (P0, X0, Y0);
  and and_3 (and_3_out, X1, Y0);
  and and_4 (and_4_out, X0, Y1);
  and and_5 (and_5_out, X1, Y1);
  and and_6 (and_6_out, X2, Y0);
  and and_7 (and_7_out, X2, Y1);
  and and_8 (and_8_out, Y2, X1);
  and and_9 (and_9_out, X2, Y2);
  Adder #(.width(1)) adder_1 (.a(and_3_out), .b(and_4_out), .out(P1), .cout(adder_1_cout));  // open: cin
  Adder #(.width(1)) adder_2 (.a(and_5_out), .b(and_6_out), .out(adder_2_out), .cout(adder_2_cout));  // open: cin
  Adder #(.width(1)) adder_3 (.a(and_7_out), .b(and_8_out), .out(adder_3_out), .cin(adder_2_cout), .cout(adder_3_cout));
  Adder #(.width(1)) adder_4 (.a(adder_3_cout), .b(and_9_out), .out(P4), .cin(adder_6_cout), .cout(P5));
  Adder #(.width(1)) adder_5 (.a(adder_2_out), .b(and_1_out), .out(P2), .cin(adder_1_cout), .cout(adder_5_cout));
  Adder #(.width(1)) adder_6 (.a(adder_3_out), .b(1'b0), .out(P3), .cin(adder_5_cout), .cout(adder_6_cout));

  // Notes on the sheet:
  //   Multiplicador de 3 bits
endmodule
