// Logisim project Somador de 4 bits com somadores de 2 bits.circ as structural Verilog: 1 circuit, main circuit main
module main (
  input  A3,
  input  A2,
  input  A1,
  input  A0,
  input  B3,
  input  B2,
  input  B1,
  input  B0,
  output CARRY,
  output S3,
  output S2,
  output S1,
  output S0
);

  wire adder_1_cout;

  Adder #(.width(2)) adder_1 (.a({B1, B0}), .b({A1, A0}), .out({S1, S0}), .cout(adder_1_cout));  // open: cin
  Adder #(.width(2)) adder_2 (.a({B3, B2}), .b({A3, A2}), .out({S3, S2}), .cin(adder_1_cout), .cout(CARRY));
endmodule
